# Fritzing sketch vaxer (saved by Fritzing 0.9.3b)

parts:
  U1 = ESP8266 NodeMCU LoLin module
  Power_plug2 = Power plug
  LED1 = LEDs [package=led10mm]
  L298N1 = L298N DC motor driver
  M1 = DC Motor
  Water_Level_Sensor1 = Water Level Sensor
  M2 = DC Motor
  Power_plug3 = Power plug
  KY-1 = Keyes Relay [package=THT]

nets:
  N1: U1.D0, KY-1.signal
  N2: U1.D2, L298N1.ENA
  N3: U1.D3, L298N1.IN1
  N4: U1.D4, L298N1.IN2
  3V3: U1.3V3, Water_Level_Sensor1.VCC, KY-1.power
  N5: U1.D5, L298N1.IN3
  N6: U1.D6, L298N1.IN4
  N7: U1.D7, L298N1.ENB
  GND: U1.GND, Power_plug2.GND, L298N1.GND, Water_Level_Sensor1.GND, KY-1.ground
  VIN: U1.Vin, L298N1.5V
  N8: U1.A0, Water_Level_Sensor1.SIG
  VCC: Power_plug2.VCC, L298N1.12V
  N9: LED1.A, KY-1.NC
  N10: LED1.C, Power_plug3.GND
  N11: L298N1.OUT1, M1.pin_2
  N12: L298N1.OUT2, M1.pin_1
  N13: L298N1.OUT3, M2.pin_2
  N14: L298N1.OUT4, M2.pin_1
  N15: Power_plug3.VCC, KY-1.C

custom parts:
  ESP8266 NodeMCU LoLin module: ESP8266 based NodeMCU
  LEDs: LEDs Standard schematic elements and footprints for 5mm, 3mm, 1206, and 0603 sized LEDs. 5mm - Spark Fun Electronics SKU : COM-00529 (and others)
  L298N DC motor driver: 2x DC motor driver with 78M05 positive voltage regulator (7..35 V) L298N: max 46 V, 2 A Set 5 V Enable jumper to enable 5 V regultor (needed for the L298N) and +5 V output at screw terminal or supply external +5 V at screw terminal Set ENA and/or ENB to +5 V to enable motor permanently or supply ENA and/or ENB with PWM signal IN1 and IN2 set rotation directory for motor A (OUT1/OUT2) IN2 and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
  Water Level Sensor: A water level sensor. This sensor operates at 3V to 5V. The Sig (signal) pin outputs an analogue signal that is in proportion to the amount of water in contact with the sensor.
  Keyes Relay: The Keyes 5V relay module is suitable for SCM development, home appliance control. It uses a 5V~12V TIL control signal which can control DC / AC signal.
